# Fritzing sketch Prototype-ESP32-FLEX-MPU-MAX (saved by Fritzing 0.9.3b)
# 18650 Li-ion Battery: CC-BY Dr Kristofer Chan, King's College London/Remote-research.org
perfboards: 2

parts:
  J8 = female pin header, 4 pins [form="♀ (female)"]
  J9 = female pin header, 4 pins [form="♀ (female)"]  # not connected
  J10 = female pin header, 8 pins [form="♀ (female)"]
  J11 = female pin header, 8 pins [form="♀ (female)"]
  J12 = female pin header, 10 pins [form="♀ (female)"]
  J13 = female pin header, 1 pin [form="♀ (female)"]  # not connected
  J14 = female pin header, 1 pin [form="♀ (female)"]  # not connected
  J15 = female pin header, 1 pin [form="♀ (female)"]
  J16 = female pin header, 1 pin [form="♀ (female)"]
  R7 = Resistor [tolerance=±5% resistance=10k package="2512 [SMD]"]
  R6 = Basic Flex Resistor
  R8 = Basic Flex Resistor  # not connected
  M7 = MakerFocus MAX30102  # not connected
  M8 = gy9250  # not connected
  BAT3 = 18650 Li-ion Battery [package=battery-18650]  # not connected
  MOD3 = MT3608 Boost No usb  # not connected
  A10 = Esp32-c3 super mini  # not connected

nets:
  N1: J8.pin2, J11.pin5
  N2: J8.pin3, J10.pin5
  N3: J8.pin4, J10.pin7, J15.pin1
  N4: J10.pin1, J12.pin3
  N5: J10.pin2, J12.pin4
  N6: J10.pin6, R6.Pin_2
  N7: J10.pin8, J16.pin1
  N8: R7.Pin_1, R6.pin_1

custom parts:
  MakerFocus MAX30102: Oximeter module using the MAX30102 chip. As usual, if you want the mounting holes in pcb, you need to drag a hole over the pad in silkscreen to actually drill the hole (by default they are not drilled)
  gy9250: MPU-9250 module (three-axis gyroscope + three-axis acceleration + three-axis magnetic field). The generic model from ebay et. al. rather than the Sparkfun version.
  18650 Li-ion Battery: 18650 li-ion Battery Standard 18650 battery with interactive connectors Creative Common Attribution 4.0 International (CC-BY 4.0) license. Any use of this part requires attribution of Dr Kristofer Chan, Department of Geography, King's College London. Contact kristofer.chan [at] kcl.ac.uk OR kris [at] remote-research.org for further information.
  MT3608 Boost No usb: Chip- MT3608 / B6289 DC to DC step up, power booster module. With adjustable output voltage. Current- 2A . || Input voltage- 2V-24V || Output voltage- 5V-28V Input interface- Inversed polarity- NO. || Led indicator- No.
  Esp32-c3 super mini: ESP32-C3 Development Board ESP32 SuperMini Development Board ESP32 Development Board WiFi Bluetooth.
